# Fritzing sketch AnalogReadAndPrint (saved by Fritzing 0.9.3b)

parts:
  RE1 = Rotary Encoder [package=THT]
  Componente1 = Arduino Leonardo (Rev3b)

nets:
  N1: RE1.EncoderPinA, Componente1.GND
  N2: RE1.EncoderPinC, Componente1.A0
  N3: RE1.EncoderPinB, Componente1.5V
