# Fritzing sketch DisplayLCD (saved by Fritzing 0.9.3b)
breadboards: 1

parts:
  LCD1 = LCD screen
  R1 = Rotary Potentiometer (Small) [maximum_resistance=100kΩ package=THT]
  Componente1 = Arduino Leonardo (Rev3b)

nets:
  VSS: LCD1.VSS, LCD1.R/W, LCD1.LED-, R1.leg2, Componente1.GND
  VDD: LCD1.VDD, LCD1.LED+, R1.leg1, Componente1.5V
  N1: LCD1.V0, R1.wiper
  N2: LCD1.RS, Componente1.D7
  N3: LCD1.E, Componente1.D8/A8
  N4: LCD1.DB4, Componente1.D9_PWM/A9
  N5: LCD1.DB5, Componente1.D10_PWM/A10
  N6: LCD1.DB6, Componente1.D11_PWM
  N7: LCD1.DB7, Componente1.D12/A11
